// Logisim project CPU(单周期).circ as structural Verilog: 8 circuits, main circuit main
module main (
  input  in_1,
  output [31:0] out_2,
  output out_3,
  output [4:0] out_4,
  output [31:0] out_5,
  output out_6,
  output [4:0] out_7,
  output [31:0] out_8
);

  wire alu_1_zero, ALUSrc, and_1_out, Branch, clock_1_out, clock_2_out, clock_3_out, MemtoReg, RegDst;
  wire [1:0] ExtOp;
  wire [2:0] ALUOp_2_0;
  wire [4:0] _20_16, _25_21;
  wire [5:0] _5_0, _31_26;
  wire [15:6] _15_0;
  wire [31:0] adder_1_out, adder_2_out, alu_1_aluresult, dm_1_out, ext_1_out, grf_1_rd1, multiplexer_1_out,
       multiplexer_3_out, multiplier_1_out;

  Multiplexer #(.width(32)) multiplexer_1 (
    .in0(adder_1_out), .in1(adder_2_out), .out(multiplexer_1_out), .sel(and_1_out));  // open: en
  Clock clock_1 (.out(clock_1_out));
  Register #(.width(32)) PC (.D(multiplexer_1_out), .Q(out_2), .clk(clock_1_out), .clr(in_1));  // open: en
  Adder #(.width(32)) adder_1 (.a(out_2), .b(32'h4), .out(adder_1_out));  // open: cin, cout
  Control_Unit control_unit_1 (
    .Op(_31_26), .Funct(_5_0), .ExtOp_1(ExtOp[1]), .ExtOp_0(ExtOp[0]), .ALUctr_2(ALUOp_2_0[2]),
    .ALUctr_1(ALUOp_2_0[1]), .ALUctr_0(ALUOp_2_0[0]), .Branch(Branch), .MemWrite(out_6), .RegWrite(out_3),
    .MemtoReg(MemtoReg), .ALUSrc(ALUSrc), .RegDst(RegDst));
  ROM #(.addrWidth(5), .dataWidth(32)) rom_1 (
    .addr(out_2[6:2]), .data({_31_26, _25_21, _20_16, _15_0, _5_0}));  // open: sel
  Multiplexer #(.width(5)) multiplexer_2 (.in0(_20_16), .in1(_15_0[15:11]), .out(out_4), .sel(RegDst));  // open: en
  EXT ext_1 (.IN({_15_0, _5_0}), .Op(ExtOp), .OUT(ext_1_out));
  Clock clock_2 (.out(clock_2_out));
  GRF grf_1 (
    .A1(_25_21), .A2(_20_16), .A3(out_4), .WD(out_5), .clk(clock_2_out), .reset(in_1), .WE(out_3),
    .RD1(grf_1_rd1), .RD2(out_8));
  ALU alu_1 (
    .SrcA(grf_1_rd1), .SrcB(multiplexer_3_out), .ALUOp_2_0(ALUOp_2_0), .ZERO(alu_1_zero),
    .ALUResult({alu_1_aluresult[31:7], out_7, alu_1_aluresult[1:0]}));
  Multiplexer #(.width(32)) multiplexer_3 (
    .in0(out_8), .in1(ext_1_out), .out(multiplexer_3_out), .sel(ALUSrc));  // open: en
  and and_1 (and_1_out, Branch, alu_1_zero);
  Multiplier #(.width(32)) multiplier_1 (.a(ext_1_out), .b(32'h4), .out(multiplier_1_out));  // open: cin, cout
  Clock clock_3 (.out(clock_3_out));
  Adder #(.width(32)) adder_2 (.a(multiplier_1_out), .b(adder_1_out), .out(adder_2_out));  // open: cin, cout
  DM dm_1 (.A(out_7), .WD(out_8), .CLK(clock_3_out), .WE(out_6), .CLR(in_1), .OUT(dm_1_out));
  Multiplexer #(.width(32)) multiplexer_4 (
    .in0({alu_1_aluresult[31:7], out_7, alu_1_aluresult[1:0]}), .in1(dm_1_out), .out(out_5), .sel(MemtoReg));  // open: en

  // Other names for the same wires on the sheet: MemAddr[4:0] = out_7; _15_0[5:0] = _5_0; _15_11[4:0] = _15_0[15:11];
  //   Instr[31:0] = out_2; MemData[31:0] = out_8; MemWrite = out_6; RegAddr[4:0] = out_4; RegData[31:0] = out_5;
  //   RegWrite = out_3; Reset = in_1

  // Notes on the sheet:
  //   contents of rom_1 (hex, n*v repeats v):
  //   341d0000 341c0000 3c01000a ac010000 34630011 ac030004 34840010 ac040008 642823 ac05000c 8c06000c
  //   8c070008 c74021 ac080010 0 1504fffe
endmodule

module IFU (
  output [31:0] out_1
);

  wire clock_1_out;
  wire [31:0] adder_1_out, register_1_q;

  Register #(.width(32)) register_1 (.D(adder_1_out), .Q(register_1_q), .clk(clock_1_out));  // open: en, clr
  Clock clock_1 (.out(clock_1_out));
  Adder #(.width(32)) adder_1 (.a(register_1_q), .b(32'h4), .out(adder_1_out));  // open: cin, cout
  ROM #(.addrWidth(5), .dataWidth(32)) rom_1 (.addr(register_1_q[6:2]), .data(out_1));  // open: sel
endmodule

module grf_prepare (
  input  [31:0] in_1,
  input  [31:0] in_2,
  input  [31:0] in_3,
  input  [31:0] _4,
  input  [31:0] in_5,
  input  [31:0] in_6,
  input  [31:0] in_7,
  input  [31:0] _8,
  input  [31:0] in_9,
  input  [31:0] _4_2,
  input  [31:0] in_11,
  input  [31:0] _12,
  input  [31:0] in_13,
  input  [31:0] in_14,
  input  [31:0] in_15,
  input  [31:0] _16,
  input  [31:0] _4_3,
  input  [31:0] in_18,
  input  [31:0] in_19,
  input  [31:0] _20,
  input  [31:0] in_21,
  input  [31:0] _4_4,
  input  [31:0] in_23,
  input  [31:0] _24,
  input  [31:0] in_25,
  input  [31:0] in_26,
  input  [31:0] in_27,
  input  [31:0] _28,
  input  [31:0] _4_5,
  input  [31:0] in_30,
  input  [31:0] _32,
  input  [31:0] in_32,
  output [31:0] out_33,
  output [31:0] out_34,
  output [31:0] out_35,
  output [31:0] out_36,
  output [31:0] out_37,
  output [31:0] out_38,
  output [31:0] out_39,
  output [31:0] out_40,
  output [31:0] out_41,
  output [31:0] out_42,
  output [31:0] out_43,
  output [31:0] out_44,
  output [31:0] out_45,
  output [31:0] out_46,
  output [31:0] out_47,
  output [31:0] out_48,
  output [31:0] out_49,
  output [31:0] out_50,
  output [31:0] out_51,
  output [31:0] out_52,
  output [31:0] out_53,
  output [31:0] out_54,
  output [31:0] out_55,
  output [31:0] out_56,
  output [31:0] out_57,
  output [31:0] out_58,
  output [31:0] out_59,
  output [31:0] out_60,
  output [31:0] out_61,
  output [31:0] out_62,
  output [31:0] out_63,
  output [31:0] out_64
);


  assign out_33 = in_1;
  assign out_34 = in_5;
  assign out_35 = in_9;
  assign out_36 = in_13;
  assign out_37 = _4_3;
  assign out_38 = in_21;
  assign out_39 = in_25;
  assign out_40 = _4_5;
  assign out_41 = in_2;
  assign out_42 = in_6;
  assign out_43 = _4_2;
  assign out_44 = in_14;
  assign out_45 = in_18;
  assign out_46 = _4_4;
  assign out_47 = in_26;
  assign out_48 = in_30;
  assign out_49 = in_3;
  assign out_50 = in_7;
  assign out_51 = in_11;
  assign out_52 = in_15;
  assign out_53 = in_19;
  assign out_54 = in_23;
  assign out_55 = in_27;
  assign out_56 = _32;
  assign out_57 = _4;
  assign out_58 = _8;
  assign out_59 = _12;
  assign out_60 = _16;
  assign out_61 = _20;
  assign out_62 = _24;
  assign out_63 = _28;
  assign out_64 = in_32;
endmodule

module GRF (
  input  clk,
  input  reset,
  input  WE,
  input  [4:0] A1,
  input  [4:0] A2,
  input  [4:0] A3,
  input  [31:0] WD,
  output [31:0] RD1,
  output [31:0] RD2
);

  wire [31:0] demultiplexer_1_out0, demultiplexer_1_out1, demultiplexer_1_out2, demultiplexer_1_out3,
       demultiplexer_1_out4, demultiplexer_1_out5, demultiplexer_1_out6, demultiplexer_1_out7,
       demultiplexer_1_out8, demultiplexer_1_out9, demultiplexer_1_out10, demultiplexer_1_out11,
       demultiplexer_1_out12, demultiplexer_1_out13, demultiplexer_1_out14, demultiplexer_1_out15,
       demultiplexer_1_out16, demultiplexer_1_out17, demultiplexer_1_out18, demultiplexer_1_out19,
       demultiplexer_1_out20, demultiplexer_1_out21, demultiplexer_1_out22, demultiplexer_1_out23,
       demultiplexer_1_out24, demultiplexer_1_out25, demultiplexer_1_out26, demultiplexer_1_out27,
       demultiplexer_1_out28, demultiplexer_1_out29, demultiplexer_1_out30, demultiplexer_1_out31,
       grf_prepare_1_out_33, grf_prepare_1_out_34, grf_prepare_1_out_35, grf_prepare_1_out_36,
       grf_prepare_1_out_37, grf_prepare_1_out_38, grf_prepare_1_out_39, grf_prepare_1_out_40,
       grf_prepare_1_out_41, grf_prepare_1_out_42, grf_prepare_1_out_43, grf_prepare_1_out_44,
       grf_prepare_1_out_45, grf_prepare_1_out_46, grf_prepare_1_out_47, grf_prepare_1_out_48,
       grf_prepare_1_out_49, grf_prepare_1_out_50, grf_prepare_1_out_51, grf_prepare_1_out_52,
       grf_prepare_1_out_53, grf_prepare_1_out_54, grf_prepare_1_out_55, grf_prepare_1_out_56,
       grf_prepare_1_out_57, grf_prepare_1_out_58, grf_prepare_1_out_59, grf_prepare_1_out_60,
       grf_prepare_1_out_61, grf_prepare_1_out_62, grf_prepare_1_out_63, grf_prepare_1_out_64,
       grf_prepare_2_out_33, grf_prepare_2_out_34, grf_prepare_2_out_35, grf_prepare_2_out_36,
       grf_prepare_2_out_37, grf_prepare_2_out_38, grf_prepare_2_out_39, grf_prepare_2_out_40,
       grf_prepare_2_out_41, grf_prepare_2_out_42, grf_prepare_2_out_43, grf_prepare_2_out_44,
       grf_prepare_2_out_45, grf_prepare_2_out_46, grf_prepare_2_out_47, grf_prepare_2_out_48,
       grf_prepare_2_out_49, grf_prepare_2_out_50, grf_prepare_2_out_51, grf_prepare_2_out_52,
       grf_prepare_2_out_53, grf_prepare_2_out_54, grf_prepare_2_out_55, grf_prepare_2_out_56,
       grf_prepare_2_out_57, grf_prepare_2_out_58, grf_prepare_2_out_59, grf_prepare_2_out_60,
       grf_prepare_2_out_61, grf_prepare_2_out_62, grf_prepare_2_out_63, grf_prepare_2_out_64, register_1_q,
       register_2_q, register_3_q, register_4_q, register_5_q, register_6_q, register_7_q, register_8_q,
       register_9_q, register_10_q, register_11_q, register_12_q, register_13_q, register_14_q,
       register_15_q, register_16_q, register_17_q, register_18_q, register_19_q, register_20_q,
       register_21_q, register_22_q, register_23_q, register_24_q, register_25_q, register_26_q,
       register_27_q, register_28_q, register_29_q, register_30_q, register_31_q, register_32_q;

  Demultiplexer #(.select(5), .width(32), .tristate("true")) demultiplexer_1 (
    .out0(demultiplexer_1_out0), .out1(demultiplexer_1_out1), .out2(demultiplexer_1_out2),
    .out3(demultiplexer_1_out3), .out4(demultiplexer_1_out4), .out5(demultiplexer_1_out5),
    .out6(demultiplexer_1_out6), .out7(demultiplexer_1_out7), .out8(demultiplexer_1_out8),
    .out9(demultiplexer_1_out9), .out10(demultiplexer_1_out10), .out11(demultiplexer_1_out11),
    .out12(demultiplexer_1_out12), .out13(demultiplexer_1_out13), .out14(demultiplexer_1_out14),
    .out15(demultiplexer_1_out15), .out16(demultiplexer_1_out16), .out17(demultiplexer_1_out17),
    .out18(demultiplexer_1_out18), .out19(demultiplexer_1_out19), .out20(demultiplexer_1_out20),
    .out21(demultiplexer_1_out21), .out22(demultiplexer_1_out22), .out23(demultiplexer_1_out23),
    .out24(demultiplexer_1_out24), .out25(demultiplexer_1_out25), .out26(demultiplexer_1_out26),
    .out27(demultiplexer_1_out27), .out28(demultiplexer_1_out28), .out29(demultiplexer_1_out29),
    .out30(demultiplexer_1_out30), .out31(demultiplexer_1_out31), .in(WD), .sel(A3));  // open: en
  Register #(.width(32)) register_1 (.D(demultiplexer_1_out0), .en(1'b0), .Q(register_1_q), .clk(clk), .clr(reset));
  Register #(.width(32)) register_2 (.D(demultiplexer_1_out8), .en(WE), .Q(register_2_q), .clk(clk), .clr(reset));
  Register #(.width(32)) register_3 (.D(demultiplexer_1_out16), .en(WE), .Q(register_3_q), .clk(clk), .clr(reset));
  Register #(.width(32)) register_4 (.D(demultiplexer_1_out24), .en(WE), .Q(register_4_q), .clk(clk), .clr(reset));
  Register #(.width(32)) register_5 (.D(demultiplexer_1_out1), .en(WE), .Q(register_5_q), .clk(clk), .clr(reset));
  Register #(.width(32)) register_6 (.D(demultiplexer_1_out9), .en(WE), .Q(register_6_q), .clk(clk), .clr(reset));
  Register #(.width(32)) register_7 (.D(demultiplexer_1_out17), .en(WE), .Q(register_7_q), .clk(clk), .clr(reset));
  Register #(.width(32)) register_8 (.D(demultiplexer_1_out25), .en(WE), .Q(register_8_q), .clk(clk), .clr(reset));
  Register #(.width(32)) register_9 (.D(demultiplexer_1_out2), .en(WE), .Q(register_9_q), .clk(clk), .clr(reset));
  Register #(.width(32)) register_10 (.D(demultiplexer_1_out10), .en(WE), .Q(register_10_q), .clk(clk), .clr(reset));
  Register #(.width(32)) register_11 (.D(demultiplexer_1_out18), .en(WE), .Q(register_11_q), .clk(clk), .clr(reset));
  Register #(.width(32)) register_12 (.D(demultiplexer_1_out26), .en(WE), .Q(register_12_q), .clk(clk), .clr(reset));
  Register #(.width(32)) register_13 (.D(demultiplexer_1_out3), .en(WE), .Q(register_13_q), .clk(clk), .clr(reset));
  Register #(.width(32)) register_14 (.D(demultiplexer_1_out11), .en(WE), .Q(register_14_q), .clk(clk), .clr(reset));
  Register #(.width(32)) register_15 (.D(demultiplexer_1_out19), .en(WE), .Q(register_15_q), .clk(clk), .clr(reset));
  Register #(.width(32)) register_16 (.D(demultiplexer_1_out27), .en(WE), .Q(register_16_q), .clk(clk), .clr(reset));
  Register #(.width(32)) register_17 (.D(demultiplexer_1_out4), .en(WE), .Q(register_17_q), .clk(clk), .clr(reset));
  Register #(.width(32)) register_18 (.D(demultiplexer_1_out12), .en(WE), .Q(register_18_q), .clk(clk), .clr(reset));
  Register #(.width(32)) register_19 (.D(demultiplexer_1_out20), .en(WE), .Q(register_19_q), .clk(clk), .clr(reset));
  Register #(.width(32)) register_20 (.D(demultiplexer_1_out28), .en(WE), .Q(register_20_q), .clk(clk), .clr(reset));
  Register #(.width(32)) register_21 (.D(demultiplexer_1_out5), .en(WE), .Q(register_21_q), .clk(clk), .clr(reset));
  Register #(.width(32)) register_22 (.D(demultiplexer_1_out13), .en(WE), .Q(register_22_q), .clk(clk), .clr(reset));
  Register #(.width(32)) register_23 (.D(demultiplexer_1_out21), .en(WE), .Q(register_23_q), .clk(clk), .clr(reset));
  Register #(.width(32)) register_24 (.D(demultiplexer_1_out29), .en(WE), .Q(register_24_q), .clk(clk), .clr(reset));
  Register #(.width(32)) register_25 (.D(demultiplexer_1_out6), .en(WE), .Q(register_25_q), .clk(clk), .clr(reset));
  Register #(.width(32)) register_26 (.D(demultiplexer_1_out14), .en(WE), .Q(register_26_q), .clk(clk), .clr(reset));
  Register #(.width(32)) register_27 (.D(demultiplexer_1_out22), .en(WE), .Q(register_27_q), .clk(clk), .clr(reset));
  Register #(.width(32)) register_28 (.D(demultiplexer_1_out30), .en(WE), .Q(register_28_q), .clk(clk), .clr(reset));
  Register #(.width(32)) register_29 (.D(demultiplexer_1_out7), .en(WE), .Q(register_29_q), .clk(clk), .clr(reset));
  Register #(.width(32)) register_30 (.D(demultiplexer_1_out15), .en(WE), .Q(register_30_q), .clk(clk), .clr(reset));
  Register #(.width(32)) register_31 (.D(demultiplexer_1_out23), .en(WE), .Q(register_31_q), .clk(clk), .clr(reset));
  Register #(.width(32)) register_32 (.D(demultiplexer_1_out31), .en(WE), .Q(register_32_q), .clk(clk), .clr(reset));
  grf_prepare grf_prepare_1 (
    .in_1(register_1_q), .in_2(register_2_q), .in_3(register_3_q), ._4(register_4_q), .in_5(register_5_q),
    .in_6(register_6_q), .in_7(register_7_q), ._8(register_8_q), .in_9(register_9_q), ._4_2(register_10_q),
    .in_11(register_11_q), ._12(register_12_q), .in_13(register_13_q), .in_14(register_14_q),
    .in_15(register_15_q), ._16(register_16_q), ._4_3(register_17_q), .in_18(register_18_q),
    .in_19(register_19_q), ._20(register_20_q), .in_21(register_21_q), ._4_4(register_22_q),
    .in_23(register_23_q), ._24(register_24_q), .in_25(register_25_q), .in_26(register_26_q),
    .in_27(register_27_q), ._28(register_28_q), ._4_5(register_29_q), .in_30(register_30_q),
    ._32(register_31_q), .in_32(register_32_q), .out_33(grf_prepare_1_out_33), .out_34(grf_prepare_1_out_34),
    .out_35(grf_prepare_1_out_35), .out_36(grf_prepare_1_out_36), .out_37(grf_prepare_1_out_37),
    .out_38(grf_prepare_1_out_38), .out_39(grf_prepare_1_out_39), .out_40(grf_prepare_1_out_40),
    .out_41(grf_prepare_1_out_41), .out_42(grf_prepare_1_out_42), .out_43(grf_prepare_1_out_43),
    .out_44(grf_prepare_1_out_44), .out_45(grf_prepare_1_out_45), .out_46(grf_prepare_1_out_46),
    .out_47(grf_prepare_1_out_47), .out_48(grf_prepare_1_out_48), .out_49(grf_prepare_1_out_49),
    .out_50(grf_prepare_1_out_50), .out_51(grf_prepare_1_out_51), .out_52(grf_prepare_1_out_52),
    .out_53(grf_prepare_1_out_53), .out_54(grf_prepare_1_out_54), .out_55(grf_prepare_1_out_55),
    .out_56(grf_prepare_1_out_56), .out_57(grf_prepare_1_out_57), .out_58(grf_prepare_1_out_58),
    .out_59(grf_prepare_1_out_59), .out_60(grf_prepare_1_out_60), .out_61(grf_prepare_1_out_61),
    .out_62(grf_prepare_1_out_62), .out_63(grf_prepare_1_out_63), .out_64(grf_prepare_1_out_64));
  grf_prepare grf_prepare_2 (
    .in_1(register_1_q), .in_2(register_2_q), .in_3(register_3_q), ._4(register_4_q), .in_5(register_5_q),
    .in_6(register_6_q), .in_7(register_7_q), ._8(register_8_q), .in_9(register_9_q), ._4_2(register_10_q),
    .in_11(register_11_q), ._12(register_12_q), .in_13(register_13_q), .in_14(register_14_q),
    .in_15(register_15_q), ._16(register_16_q), ._4_3(register_17_q), .in_18(register_18_q),
    .in_19(register_19_q), ._20(register_20_q), .in_21(register_21_q), ._4_4(register_22_q),
    .in_23(register_23_q), ._24(register_24_q), .in_25(register_25_q), .in_26(register_26_q),
    .in_27(register_27_q), ._28(register_28_q), ._4_5(register_29_q), .in_30(register_30_q),
    ._32(register_31_q), .in_32(register_32_q), .out_33(grf_prepare_2_out_33), .out_34(grf_prepare_2_out_34),
    .out_35(grf_prepare_2_out_35), .out_36(grf_prepare_2_out_36), .out_37(grf_prepare_2_out_37),
    .out_38(grf_prepare_2_out_38), .out_39(grf_prepare_2_out_39), .out_40(grf_prepare_2_out_40),
    .out_41(grf_prepare_2_out_41), .out_42(grf_prepare_2_out_42), .out_43(grf_prepare_2_out_43),
    .out_44(grf_prepare_2_out_44), .out_45(grf_prepare_2_out_45), .out_46(grf_prepare_2_out_46),
    .out_47(grf_prepare_2_out_47), .out_48(grf_prepare_2_out_48), .out_49(grf_prepare_2_out_49),
    .out_50(grf_prepare_2_out_50), .out_51(grf_prepare_2_out_51), .out_52(grf_prepare_2_out_52),
    .out_53(grf_prepare_2_out_53), .out_54(grf_prepare_2_out_54), .out_55(grf_prepare_2_out_55),
    .out_56(grf_prepare_2_out_56), .out_57(grf_prepare_2_out_57), .out_58(grf_prepare_2_out_58),
    .out_59(grf_prepare_2_out_59), .out_60(grf_prepare_2_out_60), .out_61(grf_prepare_2_out_61),
    .out_62(grf_prepare_2_out_62), .out_63(grf_prepare_2_out_63), .out_64(grf_prepare_2_out_64));
  Multiplexer #(.select(5), .width(32)) multiplexer_1 (
    .in0(grf_prepare_1_out_33), .in1(grf_prepare_1_out_34), .in2(grf_prepare_1_out_35),
    .in3(grf_prepare_1_out_36), .in4(grf_prepare_1_out_37), .in5(grf_prepare_1_out_38),
    .in6(grf_prepare_1_out_39), .in7(grf_prepare_1_out_40), .in8(grf_prepare_1_out_41),
    .in9(grf_prepare_1_out_42), .in10(grf_prepare_1_out_43), .in11(grf_prepare_1_out_44),
    .in12(grf_prepare_1_out_45), .in13(grf_prepare_1_out_46), .in14(grf_prepare_1_out_47),
    .in15(grf_prepare_1_out_48), .in16(grf_prepare_1_out_49), .in17(grf_prepare_1_out_50),
    .in18(grf_prepare_1_out_51), .in19(grf_prepare_1_out_52), .in20(grf_prepare_1_out_53),
    .in21(grf_prepare_1_out_54), .in22(grf_prepare_1_out_55), .in23(grf_prepare_1_out_56),
    .in24(grf_prepare_1_out_57), .in25(grf_prepare_1_out_58), .in26(grf_prepare_1_out_59),
    .in27(grf_prepare_1_out_60), .in28(grf_prepare_1_out_61), .in29(grf_prepare_1_out_62),
    .in30(grf_prepare_1_out_63), .in31(grf_prepare_1_out_64), .out(RD2), .sel(A2));  // open: en
  Multiplexer #(.select(5), .width(32)) multiplexer_2 (
    .in0(grf_prepare_2_out_33), .in1(grf_prepare_2_out_34), .in2(grf_prepare_2_out_35),
    .in3(grf_prepare_2_out_36), .in4(grf_prepare_2_out_37), .in5(grf_prepare_2_out_38),
    .in6(grf_prepare_2_out_39), .in7(grf_prepare_2_out_40), .in8(grf_prepare_2_out_41),
    .in9(grf_prepare_2_out_42), .in10(grf_prepare_2_out_43), .in11(grf_prepare_2_out_44),
    .in12(grf_prepare_2_out_45), .in13(grf_prepare_2_out_46), .in14(grf_prepare_2_out_47),
    .in15(grf_prepare_2_out_48), .in16(grf_prepare_2_out_49), .in17(grf_prepare_2_out_50),
    .in18(grf_prepare_2_out_51), .in19(grf_prepare_2_out_52), .in20(grf_prepare_2_out_53),
    .in21(grf_prepare_2_out_54), .in22(grf_prepare_2_out_55), .in23(grf_prepare_2_out_56),
    .in24(grf_prepare_2_out_57), .in25(grf_prepare_2_out_58), .in26(grf_prepare_2_out_59),
    .in27(grf_prepare_2_out_60), .in28(grf_prepare_2_out_61), .in29(grf_prepare_2_out_62),
    .in30(grf_prepare_2_out_63), .in31(grf_prepare_2_out_64), .out(RD1), .sel(A1));  // open: en
endmodule

module ALU (
  input  [31:0] SrcA,
  input  [31:0] SrcB,
  input  [2:0] ALUOp_2_0,
  output ZERO,
  output [31:0] ALUResult
);

  wire [31:0] adder_1_out, or_1_out, subtractor_1_out;

  Adder #(.width(32)) adder_1 (.a(SrcA), .b(SrcB), .out(adder_1_out));  // open: cin, cout
  Subtractor #(.width(32)) subtractor_1 (.a(SrcA), .b(SrcB), .out(subtractor_1_out));  // open: bin, bout
  assign or_1_out = SrcA | SrcB;  // OR_Gate or_1, 32 bits wide
  Multiplexer #(.select(3), .width(32)) multiplexer_1 (
    .in0(adder_1_out), .in1(subtractor_1_out), .in2(or_1_out), .out(ALUResult), .sel(ALUOp_2_0));  // open: in3, in4, in5, in6, in7, en
  Comparator #(.width(32)) comparator_1 (.a({32{1'b0}}), .b(ALUResult), .eq(ZERO));  // open: gt, lt

  // Other names for the same wires on the sheet: A[31:0] = SrcA; B[31:0] = SrcB
endmodule

module DM (
  input  CLK,
  input  WE,
  input  CLR,
  input  [4:0] A,
  input  [31:0] WD,
  output [31:0] OUT
);

  RAM #(.addrWidth(5), .dataWidth(32), .bus("separate")) ram_1 (
    .addr(A), .din(WD), .data(OUT), .str(WE), .sel(1'b1), .clk(CLK), .ld(1'b1), .clr(CLR));
endmodule

module Control_Unit (
  input  [5:0] Op,
  input  [5:0] Funct,
  output ExtOp_1,
  output ExtOp_0,
  output ALUctr_2,
  output ALUctr_1,
  output ALUctr_0,
  output Branch,
  output MemWrite,
  output RegWrite,
  output MemtoReg,
  output ALUSrc,
  output RegDst
);

  wire addu_out, beq_out, lui_out, lw_out, not_1_out, not_2_out, not_3_out, not_4_out, not_5_out, not_6_out,
       not_7_out, not_8_out, not_9_out, not_10_out, not_11_out, not_12_out, OP_t, or_1_out, ori_out,
       subu_out, sw_out;
  wire [5:0] multiplexer_1_out;

  Multiplexer #(.width(6)) multiplexer_1 (
    .in0({6{1'b0}}), .in1(Funct), .out(multiplexer_1_out), .sel(OP_t));  // open: en
  not not_1 (not_1_out, multiplexer_1_out[5]);
  not not_2 (not_2_out, multiplexer_1_out[4]);
  not not_3 (not_3_out, multiplexer_1_out[2]);
  not not_4 (not_4_out, multiplexer_1_out[3]);
  not not_5 (not_5_out, multiplexer_1_out[1]);
  not not_6 (not_6_out, multiplexer_1_out[0]);
  and addu (addu_out, multiplexer_1_out[5], not_2_out, not_4_out, not_3_out, not_5_out, multiplexer_1_out[0]);
  and subu (subu_out, multiplexer_1_out[5], not_2_out, not_4_out, not_3_out, multiplexer_1_out[1], multiplexer_1_out[0]);
  not not_7 (not_7_out, Op[5]);
  not not_8 (not_8_out, Op[4]);
  not not_9 (not_9_out, Op[3]);
  not not_10 (not_10_out, Op[2]);
  not not_11 (not_11_out, Op[1]);
  not not_12 (not_12_out, Op[0]);
  and ori (ori_out, not_7_out, not_8_out, Op[3], Op[2], not_11_out, Op[0]);
  and lw (lw_out, Op[5], not_8_out, not_9_out, not_10_out, Op[1], Op[0]);
  and sw (sw_out, Op[5], not_8_out, Op[3], not_10_out, Op[1], Op[0]);
  and beq (beq_out, not_7_out, not_8_out, not_9_out, Op[2], not_11_out, not_12_out);
  and lui (lui_out, not_7_out, not_8_out, Op[3], Op[2], Op[1], Op[0]);
  or or_1 (or_1_out, Op[0], Op[1], Op[2], Op[3], Op[4], Op[5]);
  not not_13 (OP_t, or_1_out);
  buf or_2 (ExtOp_1, lui_out);  // OR_Gate
  or or_3 (ExtOp_0, sw_out, beq_out, lw_out);
  buf or_4 (ALUctr_2, 1'b0);  // OR_Gate
  buf or_5 (ALUctr_1, ori_out);  // OR_Gate
  or or_6 (ALUctr_0, beq_out, subu_out);
  buf or_7 (Branch, beq_out);  // OR_Gate
  buf or_8 (MemWrite, sw_out);  // OR_Gate
  or or_9 (RegWrite, lw_out, ori_out, lui_out, subu_out, addu_out);
  or or_10 (MemtoReg, sw_out, lw_out);
  or or_11 (ALUSrc, sw_out, lw_out, lui_out, ori_out);
  or or_12 (RegDst, subu_out, addu_out);
endmodule

module EXT (
  input  [15:0] IN,
  input  [1:0] Op,
  output [31:0] OUT
);

  wire [31:0] bit_extender_1_out, bit_extender_2_out;

  assign bit_extender_1_out = {{16{1'b0}}, IN};  // Bit_Extender bit_extender_1
  assign bit_extender_2_out = {{16{IN[15]}}, IN};  // Bit_Extender bit_extender_2
  Multiplexer #(.select(2), .width(32)) multiplexer_1 (
    .in0(bit_extender_1_out), .in1(bit_extender_2_out), .in2({IN, {16{1'b0}}}), .out(OUT), .sel(Op));  // open: in3, en
endmodule
